// Logisim project SingleCycle_CPU.circ as structural Verilog
module Reg_File (
  input  [1:0] Read_Reg_1,
  input  [1:0] Read_Reg_2,
  input  [31:0] Write_Data,
  input  [1:0] Write_Reg,
  input  RegWrite,
  input  CLK,
  input  Reset,
  output [31:0] Read_Data_1,
  output [31:0] Read_Data_2
);

  wire decoder_1_out0, decoder_1_out1, decoder_1_out2, decoder_1_out3;
  wire [31:0] R0, R1, R2, R3;

  Decoder #(.select(2)) decoder_1 (
    .out0(decoder_1_out0), .out1(decoder_1_out1), .out2(decoder_1_out2), .out3(decoder_1_out3),
    .sel(Write_Reg), .en(RegWrite));
  Register #(.width(32)) u_R0 (.D({32{1'b0}}), .en(decoder_1_out0), .clk(CLK), .Q(R0), .clr(Reset));
  Register #(.width(32)) u_R1 (.D(Write_Data), .en(decoder_1_out1), .clk(CLK), .Q(R1), .clr(Reset));
  Register #(.width(32)) u_R2 (.D(Write_Data), .en(decoder_1_out2), .clk(CLK), .Q(R2), .clr(Reset));
  Register #(.width(32)) u_R3 (.D(Write_Data), .en(decoder_1_out3), .clk(CLK), .Q(R3), .clr(Reset));
  Multiplexer #(.select(2), .width(32), .enable("false")) multiplexer_1 (
    .in0(R0), .in1(R1), .in2(R2), .in3(R3), .out(Read_Data_1), .sel(Read_Reg_1));
  Multiplexer #(.select(2), .width(32), .enable("false")) multiplexer_2 (
    .in0(R0), .in1(R1), .in2(R2), .in3(R3), .out(Read_Data_2), .sel(Read_Reg_2));

  // Other names for the same wires on the sheet: ReadR1[1:0] = Read_Reg_1; ReadR2[1:0] = Read_Reg_2
endmodule

module FA_1bit (
  input  A,
  input  B,
  input  Cin,
  output Cout,
  output S
);

  wire ha_1bit_1_cout, ha_1bit_1_s, ha_1bit_2_cout;

  HA_1bit ha_1bit_1 (.A(A), .B(B), .Cout(ha_1bit_1_cout), .S(ha_1bit_1_s));
  HA_1bit ha_1bit_2 (.A(ha_1bit_1_s), .B(Cin), .Cout(ha_1bit_2_cout), .S(S));
  or or_1 (Cout, ha_1bit_1_cout, ha_1bit_2_cout);

  // Notes on the sheet:
  //   FULL-ADDER
endmodule

module HA_1bit (
  input  A,
  input  B,
  output Cout,
  output S
);

  wire and_2_out, and_3_out, not_1_out, not_2_out;

  and and_1 (Cout, A, B);
  not not_1 (not_1_out, A);
  not not_2 (not_2_out, B);
  and and_2 (and_2_out, not_1_out, B);
  and and_3 (and_3_out, A, not_2_out);
  or or_1 (S, and_2_out, and_3_out);

  // Notes on the sheet:
  //   HALF-ADDER
endmodule

module ALU_1bit (
  input  A,
  input  B,
  output R
);

  wire R_AND, R_OR;

  and and_1 (R_AND, A, B);
  or or_1 (R_OR, A, B);
  FA_1bit fa_1bit_1 (.A(A), .B(B));  // open: Cin, Cout, S
  Multiplexer #(.select(2), .enable("false")) multiplexer_1 (.out(R));  // open: in0, in1, in2, in3, sel
endmodule
